# Fritzing sketch frz (saved by Fritzing 0.9.10b)
circuit board: 8.46667cm x 5.64444cm
breadboards: 1

parts:
  HC-SR04_Sensor_1 = HC-SR04 Ultrasonic Distance Sensor
  Mod1 = Passive Buzzer
  WeMos_D1_Mini_OLED_Shield1 = WeMos D1 Mini OLED Shield
  元件1 = Arduino Uno (Rev3)

nets:
  VCC: HC-SR04_Sensor_1.VCC, Mod1.S, 元件1.5V
  N1: HC-SR04_Sensor_1.TRIG, 元件1.D4
  N2: HC-SR04_Sensor_1.ECHO, 元件1.D3_PWM
  GND: HC-SR04_Sensor_1.GND, Mod1.-, WeMos_D1_Mini_OLED_Shield1.D4, 元件1.GND
  N3: Mod1.NC, 元件1.D2
  N4: WeMos_D1_Mini_OLED_Shield1.D1, 元件1.D11_PWM/MOSI
  N5: WeMos_D1_Mini_OLED_Shield1.D2, 元件1.D10_PWM/SS
  N6: WeMos_D1_Mini_OLED_Shield1.D3, 元件1.D9_PWM
  N7: WeMos_D1_Mini_OLED_Shield1.G, 元件1.3V3
  N8: WeMos_D1_Mini_OLED_Shield1.RX, 元件1.D12/MISO
  N9: WeMos_D1_Mini_OLED_Shield1.TX, 元件1.D13/SCK

notes:
  7个引脚分别为
  RES, CS,DC, D0, D9,GND,VCC
